// Logisim project smips.circ as structural Verilog
module Board (
);

  wire CLK, HALT, MEM_WE, RESET, TTY_WE;
  wire [3:0] MEM_BE;
  wire [6:0] TTY_DATA;
  wire [31:0] MEM_ADDR, MEM_RDATA, MEM_WDATA;

  Clock Reloj (.out(CLK));
  Button u_Reset (.out(RESET));
  CPU cpu_1 (
    .CLK(CLK), .RESET(RESET), .MEM_RDATA(MEM_RDATA), .MEM_ADDR(MEM_ADDR), .MEM_WDATA(MEM_WDATA),
    .MEM_BE(MEM_BE), .MEM_WE(MEM_WE), .TTY_DATA(TTY_DATA), .TTY_WE(TTY_WE), .HALT(HALT));
  TTY #(.cols(48), .rows(12)) tty_1 (.data(TTY_DATA), .clk(CLK), .we(TTY_WE), .clr(RESET));
  Memory memory_1 (.CLK(CLK), .ADDR(MEM_ADDR), .WDATA(MEM_WDATA), .BE(MEM_BE), .WE(MEM_WE), .RDATA(MEM_RDATA));
  LED u_Halt (.in(HALT));

  // Notes on the sheet:
  //   S-MIPS | Board
  //   No modificar: la CPU se implementa dentro del subcircuito CPU.
endmodule

module CPU (
  input  CLK,
  input  [31:0] MEM_ADDR,
  input  RESET,
  input  [31:0] MEM_WDATA,
  input  [31:0] MEM_RDATA,
  input  [3:0] MEM_BE,
  input  MEM_WE,
  input  [6:0] TTY_DATA,
  input  TTY_WE,
  input  HALT
);

  Datapath datapath_1 ();  // open: in_12, in_16, in_1, in_2, in_4, in_6, in_8, in_10, in_14, in_11, in_13, in_15, in_3, in_5, in_7, in_9, out_17, out_18

  // Notes on the sheet:
  //   CPU S-MIPS: implementar aqui
  //   No cambiar nombres, anchos ni sentido de los pines: la placa depende de ellos.
endmodule

module Memory (
  input  CLK,
  input  [31:0] RDATA,
  input  [31:0] ADDR,
  input  [31:0] WDATA,
  input  [3:0] BE,
  input  WE
);

  RAM #(.addrWidth(12), .dataWidth(32)) ram_1 (
    .addr(ADDR[13:2]), .we(WE), .oe(1'b1), .clk(CLK), .din(WDATA), .dout(RDATA));

  // Other names for the same wires on the sheet: A[11:0] = ADDR[13:2]

  // Notes on the sheet:
  //   Memoria unificada: 4096 palabras de 32 bits (16 KiB), little-endian
  //   Lectura combinacional; escritura en el flanco de subida de CLK con WE=1, solo en los bytes con BE=1.
  //   Se usan los bits 13..2 de ADDR; los demas se ignoran (el espacio se repite cada 16 KiB).
endmodule

module ALU (
  input  [2:0] in_1,
  input  [31:0] in_2,
  input  [31:0] in_3,
  input  in_4,
  output [31:0] out_5,
  output ZeroF
);

  wire comparator_1_lt;
  wire [31:0] ADD, AND, COMP_SIGNED, LOGICAL_LEFT, LOGICAL_RIGHT, MINUS, OR;

  // Probe on in_2
  // Probe on in_2
  Adder #(.width(32)) adder_1 (.a(in_2), .b(in_3), .out(ADD));  // open: cin, cout
  Subtractor #(.width(32)) subtractor_1 (.a(in_2), .b(in_3), .out(MINUS));  // open: bin, bout
  Comparator #(.width(32)) comparator_1 (.a(in_2), .b(in_3), .lt(comparator_1_lt));  // open: gt, eq
  Shifter #(.shift("lr"), .width(32)) shifter_1 (.in(in_2), .\dist (in_3[4:0]), .out(LOGICAL_LEFT));
  Shifter #(.shift("lr"), .width(32)) shifter_2 (.in(in_2), .\dist (in_3[4:0]), .out(LOGICAL_RIGHT));
  // Probe on in_3
  // Probe on in_3
  assign AND = in_2 & in_3;  // AND_Gate and_1, 32 bits wide
  assign OR = in_2 | in_3;  // OR_Gate or_1, 32 bits wide
  assign COMP_SIGNED = {{31{comparator_1_lt}}, comparator_1_lt};  // Bit_Extender bit_extender_1
  // Probe on in_1
  // Probe on out_5
  // Probe on out_5
  Multiplexer #(.enable("true"), .select(3), .width(32)) multiplexer_1 (
    .in0(ADD), .in1(MINUS), .in2(AND), .in3(OR), .in4(COMP_SIGNED), .in5(LOGICAL_LEFT), .in6(LOGICAL_RIGHT),
    .in7(in_3), .out(out_5), .sel(in_1));  // open: en
  Comparator #(.width(32)) comparator_2 (.a({32{1'b0}}), .b(out_5), .eq(ZeroF));  // open: gt, lt

  // Other names for the same wires on the sheet: A[31:0] = in_2; B[31:0] = in_3; CLK = in_4; MAIN[31:0] = out_5;
  //   OP[2:0] = in_1; ZERO = ZeroF

  // Notes on the sheet:
  //   000
  //   001
  //   010
  //   011
  //   100
  //   0101
  //   110
  //   INPUTS
  //   OUTPUTS
  //   COMBINATIONAL LOGIC
endmodule

module Decoder (
  input  [1:0] ALUop,
  input  [5:0] FUNCT,
  output [2:0] OP
);

  ROM #(.dataWidth(3)) rom_1 (.addr({FUNCT, ALUop}), .data(OP));

  // Notes on the sheet:
  //   contents of rom_1 (hex, n*v repeats v):
  //   64*0 64*1 5 0 6 31*0 1 0 2 3 4*0 4
endmodule

module Datapath (
  input  in_1,
  input  in_2,
  input  in_3,
  input  in_4,
  input  in_5,
  input  in_6,
  input  in_7,
  input  in_8,
  input  in_9,
  input  [1:0] in_10,
  input  in_11,
  input  in_12,
  input  in_13,
  input  [3:0] in_14,
  input  in_15,
  input  [1:0] in_16,
  output [5:0] out_17,
  output out_18
);

  wire [2:0] ALUOP;
  wire [4:0] wa;
  wire [5:0] Funct, funct_t;
  wire [15:6] Inm;
  wire [25:16] IR;
  wire [31:0] A, ALUOUT, B, InA, InB, IorD_out, MDR, PCOUT, RALU, rd1, rd2, RDATA, sign_ext, wd;

  Register #(.width(32)) PC (.D(ALUOUT), .en(in_3), .clk(in_1), .Q(PCOUT));  // open: clr
  Register #(.width(32)) u_IR (.D(RDATA), .en(in_7), .clk(in_1), .Q({out_17, IR, Inm, funct_t}));  // open: clr
  Register #(.width(32)) u_A (.D(rd1), .en(in_9), .clk(in_1), .Q(A));  // open: clr
  Register #(.width(32)) u_B (.D(rd2), .en(in_11), .clk(in_1), .Q(B));  // open: clr
  Decoder decoder_1 (.ALUop(in_16), .FUNCT(Funct), .OP(ALUOP));
  assign sign_ext = {{16{Inm[15]}}, {Inm, funct_t}};  // Bit_Extender bit_extender_1
  Register #(.width(32)) u_ALUOUT (.D(ALUOUT), .en(in_15), .clk(in_1), .Q(RALU));  // open: clr
  Register #(.width(32)) u_MDR (.D(RDATA), .en(in_13), .clk(in_1), .Q(MDR));  // open: clr
  ALU alu_1 (.in_2(InA), .in_3(InB), .in_4(in_1), .in_1(ALUOP), .out_5(ALUOUT), .ZeroF(out_18));
  Multiplexer #(.width(5)) multiplexer_1 (.in0(IR[20:16]), .in1(Inm[15:11]), .out(wa), .sel(in_4));
  Multiplexer #(.width(32)) multiplexer_2 (.in0(PCOUT), .in1(ALUOUT), .out(IorD_out), .sel(in_2));
  Multiplexer #(.width(32)) multiplexer_3 (.in0(RALU), .in1(MDR), .out(wd), .sel(in_6));
  register_file register_file_1 (
    .clk(in_1), .we(in_5), .wa(wa), .wd(wd), .ra1(IR[25:21]), .ra2(IR[20:16]), .rd1(rd1), .rd2(rd2));  // open: rst
  Multiplexer #(.width(32)) multiplexer_4 (.in0(PCOUT), .in1(A), .out(InA), .sel(in_8));
  Multiplexer #(.select(2), .width(32)) multiplexer_5 (
    .in0(B), .in1(32'h100), .in2(sign_ext), .out(InB), .sel(in_10));  // open: in3
  Memory memory_1 (.CLK(in_1), .ADDR(IorD_out), .WDATA(B), .BE(in_14), .WE(in_12), .RDATA(RDATA));

  // Other names for the same wires on the sheet: ALUSrcA = in_8; ALUSrcB[1:0] = in_10; ALUwr = in_15; Awr = in_9;
  //   BE[3:0] = in_14; Bwr = in_11; clk = in_1; InOp[1:0] = in_16; IorD = in_2; Inm[5:0] = funct_t;
  //   IR (some bits) = {out_17, Inm, funct_t}; rd[4:0] = Inm[15:11]; rt[4:0] = IR[20:16]; rs[4:0] = IR[25:21];
  //   op[5:0] = out_17; IRwr = in_7; MDRwr = in_13; MemToReg = in_6; MemWrite = in_12; PCwr = in_3; RegDst = in_4;
  //   Regwr = in_5; ZeroF = out_18

  // Notes on the sheet:
  //   Direcciones
  //   Funct
  //   rd
  //   rt
  //   rs
  //   op
  //   INPUTS
  //   Reg Helpers
  //   ALU
  //   Decoder
  //   SIGN EXTENSION
  //   OUTPUTS
  //   REG FILE
  //   MUX Helpers
endmodule

module FSM (
  input  in_1,
  input  [5:0] in_2,
  input  in_3,
  input  in_4,
  output out_5,
  output out_6,
  output out_7,
  output out_8,
  output [1:0] out_9,
  output out_10,
  output [3:0] out_11,
  output [1:0] out_12,
  output out_13,
  output out_14,
  output out_15,
  output out_16,
  output out_17,
  output out_18,
  output out_19
);

  wire and_1_out, beq, lw, or_1_out, sw;
  wire [2:1] I1;
  wire [3:0] Dstate, I2, Qstate;

  Multiplexer #(.select(4)) multiplexer_1 (
    .in0(1'b0), .in1(1'b0), .in2(1'b1), .in3(1'b0), .in4(1'b0), .in5(1'b0), .in6(1'b1), .in7(1'b0),
    .in8(1'b1), .in9(1'b0), .in10(1'b0), .in11(1'b0), .in12(1'b0), .in13(1'b0), .in14(1'b0), .in15(1'b0),
    .out(out_8), .sel(Qstate));
  Register #(.width(4)) register_1 (.D(Dstate), .clk(in_1), .Q(Qstate), .clr(in_4));  // open: en
  or or_1 (or_1_out, out_13, and_1_out);
  and and_1 (and_1_out, in_3, out_11[3]);
  Multiplexer #(.select(4), .width(2)) multiplexer_2 (
    .in0(2'b01), .in1(2'b11), .in2(2'b10), .in3(2'b00), .in4(2'b00), .in5(2'b00), .in6(2'b00), .in7(2'b00),
    .in8(2'b00), .in9(2'b00), .in10(2'b00), .in11(2'b00), .in12(2'b00), .in13(2'b00), .in14(2'b00),
    .in15(2'b00), .out(out_9), .sel(Qstate));
  Multiplexer #(.select(4)) multiplexer_3 (
    .in0(1'b1), .in1(1'b0), .in2(1'b0), .in3(1'b0), .in4(1'b0), .in5(1'b0), .in6(1'b0), .in7(1'b0),
    .in8(or_1_out), .in9(1'b0), .in10(1'b0), .in11(1'b0), .in12(1'b0), .in13(1'b0), .in14(1'b0), .in15(1'b0),
    .out(out_13), .sel(Qstate));
  Multiplexer #(.select(4)) multiplexer_4 (
    .in0(1'b0), .in1(1'b0), .in2(1'b0), .in3(1'b0), .in4(1'b0), .in5(1'b0), .in6(1'b0), .in7(1'b1),
    .in8(1'b0), .in9(1'b0), .in10(1'b0), .in11(1'b0), .in12(1'b0), .in13(1'b0), .in14(1'b0), .in15(1'b0),
    .out(out_6), .sel(Qstate));
  Comparator #(.width(6)) comparator_1 (.a(in_2), .b({6{1'b0}}), .eq(I1[2]));  // open: gt, lt
  Comparator #(.width(6)) comparator_2 (.a(in_2), .b(6'b100011), .eq(lw));  // open: gt, lt
  Multiplexer #(.select(4)) multiplexer_5 (
    .in0(1'b0), .in1(1'b0), .in2(1'b0), .in3(1'b0), .in4(1'b0), .in5(1'b1), .in6(1'b0), .in7(1'b0),
    .in8(1'b0), .in9(1'b0), .in10(1'b0), .in11(1'b0), .in12(1'b0), .in13(1'b0), .in14(1'b0), .in15(1'b0),
    .out(out_10), .sel(Qstate));
  Multiplexer #(.select(4)) multiplexer_6 (
    .in0(1'b0), .in1(1'b0), .in2(1'b0), .in3(1'b0), .in4(1'b1), .in5(1'b0), .in6(1'b0), .in7(1'b0),
    .in8(1'b0), .in9(1'b0), .in10(1'b0), .in11(1'b0), .in12(1'b0), .in13(1'b0), .in14(1'b0), .in15(1'b0),
    .out(out_7), .sel(Qstate));
  Multiplexer #(.select(4), .width(2)) multiplexer_7 (
    .in0(2'b00), .in1(2'b00), .in2(2'b00), .in3(2'b00), .in4(2'b00), .in5(2'b00), .in6(2'b10), .in7(2'b00),
    .in8(2'b01), .in9(2'b00), .in10(2'b00), .in11(2'b00), .in12(2'b00), .in13(2'b00), .in14(2'b00),
    .in15(2'b00), .out(out_12), .sel(Qstate));
  Comparator #(.width(6)) comparator_3 (.a(in_2), .b(6'b101011), .eq(sw));  // open: gt, lt
  Comparator #(.width(6)) comparator_4 (.a(in_2), .b(6'b000100), .eq(beq));  // open: gt, lt
  Multiplexer #(.select(4)) multiplexer_8 (
    .in0(1'b1), .in1(1'b0), .in2(1'b0), .in3(1'b0), .in4(1'b0), .in5(1'b0), .in6(1'b0), .in7(1'b0),
    .in8(1'b0), .in9(1'b0), .in10(1'b0), .in11(1'b0), .in12(1'b0), .in13(1'b0), .in14(1'b0), .in15(1'b0),
    .out(out_15), .sel(Qstate));
  Multiplexer #(.select(4)) multiplexer_9 (
    .in0(1'b0), .in1(1'b1), .in2(1'b0), .in3(1'b0), .in4(1'b0), .in5(1'b0), .in6(1'b0), .in7(1'b0),
    .in8(1'b0), .in9(1'b0), .in10(1'b0), .in11(1'b0), .in12(1'b0), .in13(1'b0), .in14(1'b0), .in15(1'b0),
    .out(out_16), .sel(Qstate));
  or or_2 (I1[1], beq, I1[2]);
  Multiplexer #(.select(4)) multiplexer_10 (
    .in0(1'b0), .in1(1'b0), .in2(1'b0), .in3(1'b0), .in4(1'b1), .in5(1'b0), .in6(1'b0), .in7(1'b1),
    .in8(1'b0), .in9(1'b0), .in10(1'b0), .in11(1'b0), .in12(1'b0), .in13(1'b0), .in14(1'b0), .in15(1'b0),
    .out(out_14), .sel(Qstate));
  Multiplexer #(.select(4)) multiplexer_11 (
    .in0(1'b0), .in1(1'b0), .in2(1'b0), .in3(1'b1), .in4(1'b0), .in5(1'b0), .in6(1'b0), .in7(1'b0),
    .in8(1'b0), .in9(1'b0), .in10(1'b0), .in11(1'b0), .in12(1'b0), .in13(1'b0), .in14(1'b0), .in15(1'b0),
    .out(out_18), .sel(Qstate));
  Multiplexer #(.select(4), .width(4)) multiplexer_12 (
    .in0(4'b0001), .in1({beq, I1, 1'b0}), .in2(I2), .in3(4'b0100), .in4(4'b0000), .in5(4'b0000),
    .in6(4'b0111), .in7(4'b0000), .in8(4'b0000), .in9(4'b0000), .in10(4'b0000), .in11(4'b0000),
    .in12(4'b0000), .in13(4'b0000), .in14(4'b0000), .in15(4'b0000), .out(Dstate), .sel(Qstate));
  Multiplexer #(.select(4)) multiplexer_13 (
    .in0(1'b0), .in1(1'b0), .in2(1'b0), .in3(1'b1), .in4(1'b0), .in5(1'b1), .in6(1'b0), .in7(1'b0),
    .in8(1'b0), .in9(1'b0), .in10(1'b0), .in11(1'b0), .in12(1'b0), .in13(1'b0), .in14(1'b0), .in15(1'b0),
    .out(out_5), .sel(Qstate));
  Multiplexer #(.width(4)) multiplexer_14 (.in0(4'b0011), .in1(4'b0101), .out(I2), .sel(sw));
  Multiplexer #(.select(4)) multiplexer_15 (
    .in0(1'b0), .in1(1'b0), .in2(1'b1), .in3(1'b0), .in4(1'b0), .in5(1'b0), .in6(1'b1), .in7(1'b0),
    .in8(1'b0), .in9(1'b0), .in10(1'b0), .in11(1'b0), .in12(1'b0), .in13(1'b0), .in14(1'b0), .in15(1'b0),
    .out(out_19), .sel(Qstate));

  assign out_17 = out_16;

  // Other names for the same wires on the sheet: ALUSrcA = out_8; ALUSrcB[1:0] = out_9; ALUwr = out_19;
  //   BE[3:0] = out_11; Awr = out_16; Bwr = out_16; clk = in_1; R = I1[2]; I1[3] = beq; InOp[1:0] = out_12;
  //   IRoD = out_5; IRwr = out_15; MDRwr = out_18; MemToReg = out_7; MemWrite = out_10; op[5:0] = in_2; PCwr = out_13;
  //   RegDst = out_6; Regwr = out_14; RST = in_4; ZeroF = in_3

  // Notes on the sheet:
  //   INPUTS
  //   OUTPUTS
  //   STATES
  //   COMBINATIONAL LOGIC
endmodule

module TEST (
);

  wire clock_1_out, datapath_1_out_18, fsm_1_out_5, fsm_1_out_6, fsm_1_out_7, fsm_1_out_8, fsm_1_out_10,
       fsm_1_out_13, fsm_1_out_14, fsm_1_out_15, fsm_1_out_16, fsm_1_out_17, fsm_1_out_18, fsm_1_out_19;
  wire [1:0] fsm_1_out_9, fsm_1_out_12;
  wire [3:0] fsm_1_out_11;
  wire [5:0] datapath_1_out_17;

  Clock clock_1 (.out(clock_1_out));
  FSM fsm_1 (
    .in_2(datapath_1_out_17), .in_1(clock_1_out), .in_3(datapath_1_out_18), .out_13(fsm_1_out_13),
    .out_14(fsm_1_out_14), .out_15(fsm_1_out_15), .out_16(fsm_1_out_16), .out_17(fsm_1_out_17),
    .out_19(fsm_1_out_19), .out_18(fsm_1_out_18), .out_11(fsm_1_out_11), .out_12(fsm_1_out_12),
    .out_5(fsm_1_out_5), .out_6(fsm_1_out_6), .out_7(fsm_1_out_7), .out_8(fsm_1_out_8), .out_9(fsm_1_out_9),
    .out_10(fsm_1_out_10));  // open: in_4
  Datapath datapath_1 (
    .in_12(fsm_1_out_10), .in_16(fsm_1_out_12), .in_1(clock_1_out), .in_2(fsm_1_out_5), .in_4(fsm_1_out_6),
    .in_6(fsm_1_out_7), .in_8(fsm_1_out_8), .in_10(fsm_1_out_9), .in_14(fsm_1_out_11), .in_11(fsm_1_out_17),
    .in_13(fsm_1_out_18), .in_15(fsm_1_out_19), .in_3(fsm_1_out_13), .in_5(fsm_1_out_14),
    .in_7(fsm_1_out_15), .in_9(fsm_1_out_16), .out_17(datapath_1_out_17), .out_18(datapath_1_out_18));
endmodule

// VHDL entity register_file, as the project stores it:
library ieee;
use ieee.std_logic_1164.all;
use ieee.numeric_std.all;
entity register_file is
    port (
        clk   : in  std_logic;
        rst   : in  std_logic;
        we    : in  std_logic;                      -- Write Enable
        wa    : in  std_logic_vector(4 downto 0);   -- Write Address (rd / rt)
        wd    : in  std_logic_vector(31 downto 0);  -- Write Data
        ra1   : in  std_logic_vector(4 downto 0);   -- Read Address 1 (rs)
        ra2   : in  std_logic_vector(4 downto 0);   -- Read Address 2 (rt)
        rd1   : out std_logic_vector(31 downto 0);  -- Read Data 1
        rd2   : out std_logic_vector(31 downto 0)   -- Read Data 2
    );
end entity register_file;

architecture rtl of register_file is
    -- Definición del banco de 32 registros de 32 bits
    type reg_array is array (0 to 31) of std_logic_vector(31 downto 0);
    signal regs : reg_array;
begin

    -- Puerto de lectura 1 (Combinacional / Asíncrono)
    -- Si la dirección es 0 ($zero), retorna siempre 0.
    process(ra1, regs)
    begin
        if to_integer(unsigned(ra1)) = 0 then
            rd1 <= (others => '0');
        else
            rd1 <= regs(to_integer(unsigned(ra1)));
        end if;
    end process;

    -- Puerto de lectura 2 (Combinacional / Asíncrono)
    -- Si la dirección es 0 ($zero), retorna siempre 0.
    process(ra2, regs)
    begin
        if to_integer(unsigned(ra2)) = 0 then
            rd2 <= (others => '0');
        else
            rd2 <= regs(to_integer(unsigned(ra2)));
        end if;
    end process;

    -- Puerto de escritura (Síncrono al flanco de subida del reloj)
    process(clk)
    begin
        if rising_edge(clk) then
            if rst = '1' then
                -- Inicialización por reset según especificación [R6]
                for i in 0 to 31 loop
                    regs(i) <= (others => '0');
                end loop;
                regs(28) <= x"00001800"; -- $gp inicial = 0x1800[span_5](start_span)[span_5](end_span)[span_6](start_span)[span_6](end_span)
                regs(29) <= x"00003FFC"; -- $sp inicial = 0x3FFC[span_7](start_span)[span_7](end_span)[span_8](start_span)[span_8](end_span)
            else
                -- Escritura condicional (el registro $zero / $0 nunca se modifica)
                if we = '1' and to_integer(unsigned(wa)) /= 0 then
                    regs(to_integer(unsigned(wa))) <= wd;
                end if;
                -- Garantizar por seguridad que $zero permanezca en 0
                regs(0) <= (others => '0');
            end if;
        end if;
    end process;
end architecture rtl;
